# Fritzing sketch board (saved by Fritzing 0.9.3b)
breadboards: 1

parts:
  Part1 = Arduino Nano (Rev3.0)
  U1 = 74HC595 [package="DIP16 [THT]"]
  R1 = Resistor [tolerance=±5% resistance=330 package=THT]  # not connected
  R2 = Resistor [tolerance=±5% resistance=330 package=THT]
  R3 = Resistor [tolerance=±5% resistance=330 package=THT]
  R4 = Resistor [tolerance=±5% resistance=330 package=THT]
  R5 = Resistor [tolerance=±5% resistance=330 package=THT]
  R6 = Resistor [tolerance=±5% resistance=330 package=THT]
  R7 = Resistor [tolerance=±5% resistance=330 package=THT]
  R8 = Resistor [tolerance=±5% resistance=330 package=THT]
  LED1 = LED - 5mm [color="Red (633nm)" package="5 mm [THT]"]
  LED2 = LED - 5mm [color="Red (633nm)" package="5 mm [THT]"]
  LED3 = LED - 5mm [color="Red (633nm)" package="5 mm [THT]"]
  LED4 = LED - 5mm [color="Red (633nm)" package="5 mm [THT]"]
  LED5 = LED - 5mm [color="Red (633nm)" package="5 mm [THT]"]
  LED6 = LED - 5mm [color="Red (633nm)" package="5 mm [THT]"]
  LED7 = LED - 5mm [color="Red (633nm)" package="5 mm [THT]"]
  LED8 = LED - 5mm [color="Red (633nm)" package="5 mm [THT]"]

nets:
  GND: Part1.GND, U1.GND, LED1.anode, LED2.anode, LED3.anode, LED4.anode, LED5.anode, LED6.anode, LED7.anode, LED8.anode
  N1: Part1.D2, U1.DS
  N2: Part1.D3, U1.OE
  N3: Part1.D4, U1.ST_CP
  N4: Part1.D5, U1.SH_CP
  N5: Part1.D6, U1.MR
  5V: Part1.5V, U1.VCC
  N6: U1.Q1, R7.Pin_1
  N7: U1.Q2, R6.Pin_1
  N8: U1.Q3, R5.Pin_1
  N9: U1.Q4, R4.Pin_1
  N10: U1.Q5, R3.Pin_1
  N11: U1.Q6, R2.Pin_1
  N12: U1.Q0, R8.Pin_1
  N13: R2.Pin_0, LED7.cathode
  N14: R3.Pin_0, LED6.cathode
  N15: R4.Pin_0, LED5.cathode
  N16: R5.Pin_0, LED4.cathode
  N17: R6.Pin_0, LED1.cathode
  N18: R7.Pin_0, LED3.cathode
  N19: R8.Pin_0, LED2.cathode
